// Logisim project LOGISM-Heatwatch.circ as structural Verilog: 1 circuit, main circuit main
module main (
  input  S1,
  input  [10:0] SENSOR,
  input  in_3,
  input  COUNTER,
  input  [10:0] in_5,
  output [10:0] out_6,
  output out_7,
  output [10:0] out_8,
  output [10:0] out_9
);

  wire CLK_out;
  wire [10:0] adder_1_out, counter_1_q, d_ff_1_q, multiplier_1_out, subtractor_1_out;

  Clock #(.lowDuration(30)) CLK (.out(CLK_out));
  Counter #(.width(11), .max('h7ff)) counter_1 (.Q(counter_1_q), .clk(CLK_out));  // open: load, D, count, carry, clr
  Divider #(.width(11)) divider_1 (.a(adder_1_out), .b(counter_1_q), .out(out_9));  // open: upper, rem
  Adder #(.width(11)) adder_1 (.a(out_6), .b(multiplier_1_out), .out(adder_1_out));  // open: cin, cout
  Counter #(.width(11), .max('h7ff)) COUNTER_2 (
    .load(S1), .D(SENSOR), .count(in_3), .Q(out_6), .carry(out_7), .clk(CLK_out), .clr(COUNTER));
  Subtractor #(.width(11)) subtractor_1 (.a(counter_1_q), .b(in_5), .out(subtractor_1_out));  // open: bin, bout
  Multiplier #(.width(11)) multiplier_1 (
    .a(subtractor_1_out), .b(d_ff_1_q), .out(multiplier_1_out));  // open: cin, cout
  D_Flip_Flop d_ff_1 (.clk(CLK_out), .D(out_9[0]), .Q(d_ff_1_q[0]));  // open: Qn, preset, en, reset
  D_Flip_Flop d_ff_2 (.clk(CLK_out), .D(out_9[1]), .Q(d_ff_1_q[1]));  // open: Qn, preset, en, reset
  D_Flip_Flop d_ff_3 (.clk(CLK_out), .D(out_9[2]), .Q(d_ff_1_q[2]));  // open: Qn, preset, en, reset
  D_Flip_Flop d_ff_4 (.clk(CLK_out), .D(out_9[3]), .Q(d_ff_1_q[3]));  // open: Qn, preset, en, reset
  D_Flip_Flop d_ff_5 (.clk(CLK_out), .D(out_9[4]), .Q(d_ff_1_q[4]));  // open: Qn, preset, en, reset
  D_Flip_Flop d_ff_6 (.clk(CLK_out), .D(out_9[5]), .Q(d_ff_1_q[5]));  // open: Qn, preset, en, reset
  D_Flip_Flop d_ff_7 (.clk(CLK_out), .D(out_9[6]), .Q(d_ff_1_q[6]));  // open: Qn, preset, en, reset
  D_Flip_Flop d_ff_8 (.clk(CLK_out), .D(out_9[7]), .Q(d_ff_1_q[7]));  // open: Qn, preset, en, reset
  D_Flip_Flop d_ff_9 (.clk(CLK_out), .D(out_9[8]), .Q(d_ff_1_q[8]));  // open: Qn, preset, en, reset
  D_Flip_Flop d_ff_10 (.clk(CLK_out), .D(out_9[9]), .Q(d_ff_1_q[9]));  // open: Qn, preset, en, reset
  D_Flip_Flop d_ff_11 (.clk(CLK_out), .D(out_9[10]), .Q(d_ff_1_q[10]));  // open: Qn, preset, en, reset

  assign out_8 = SENSOR;

  // Notes on the sheet:
  //   INSTRUCTIONS:
  //   1. SET S1 TO HIGH
  //   3.GIVE INPUT VALUE AT THE SENSOR
  //   4.GIVE CLOCK PULSE AFTER THE INPUT
  //   5.TURN OFF THE CLOCK PULSE
  //   6.REPEAT THE PROCESS FROM STEP 3
  //   ADDER
  //   DIVIDER
  //   2. SET ONE OF THE INPUTS OF THE SUBTRACTOR TO 1
  //   SUBTRACTOR
  //   HEAT WATCH:TEMPERATURE MONITORING SYSYTEM
  //   MULTIPLIER
  //   ARRAY OF D-FLIP FLOPS
  //   CURRENT TEMPERATURE
  //   AVERAGE TEMPERATURE
endmodule
